// Logisim project project.circ as structural Verilog: 1 circuit, main circuit main
module main (
  output [15:0] out_1
);

  wire and_1_out, and_2_out, and_5_out, and_6_out, and_7_out, and_8_out, and_9_out, avail, cdm_16_1_p3, clk,
       clr_tty1, clr_tty2, dmplxr, io_en, keyboard_1_avail, mem, not_1_out, r_w_prime, random,
       read_en_keyboard, word, write_en_tty1, write_en_tty2;
  wire [6:0] keyboard_1_data;
  wire [7:0] random_1_out;
  wire [15:0] addr, bit_extender_1_out, bit_extender_2_out, bit_extender_3_out, data, in, out;

  // CdM_16 cdm_16_1: pin names not known; wires that end beside it: clk, out_1, cdm_16_1_p3, cdm_16_1_p3, mem, r_w_prime, word, addr, out, in
  Clock clock_1 (.out(clk));
  assign in = r_w_prime ? data : 16'bz;  // Controlled_Buffer controlled_buffer_1
  Keyboard #(.trigger("falling")) keyboard_1 (
    .clk(clk), .re(and_1_out), .avail(keyboard_1_avail), .data(keyboard_1_data));  // open: clr
  assign data = not_1_out ? out : 16'bz;  // Controlled_Buffer controlled_buffer_2
  not not_1 (not_1_out, r_w_prime);
  and and_1 (and_1_out, io_en, r_w_prime, read_en_keyboard);
  // Debugger debugger_1: pin names not known
  assign bit_extender_1_out = {{15{1'b0}}, keyboard_1_avail};  // Bit_Extender bit_extender_1
  assign data = and_1_out ? bit_extender_2_out : 16'bz;  // Controlled_Buffer controlled_buffer_3
  assign bit_extender_2_out = {{9{1'b0}}, keyboard_1_data};  // Bit_Extender bit_extender_2
  assign data = and_2_out ? bit_extender_1_out : 16'bz;  // Controlled_Buffer controlled_buffer_4
  and and_2 (and_2_out, io_en, r_w_prime, avail);
  Comparator #(.width(16), .mode("unsigned")) comparator_1 (.a(addr), .b(16'h800a), .eq(random));  // open: gt, lt
  Comparator #(.width(16), .mode("unsigned")) comparator_2 (.a(addr), .b(16'h8008), .eq(clr_tty2));  // open: gt, lt
  Comparator #(.width(16), .mode("unsigned")) comparator_3 (.a(addr), .b(16'h8006), .eq(clr_tty1));  // open: gt, lt
  Comparator #(.width(16), .mode("unsigned")) comparator_4 (.a(addr), .b(16'h8005), .eq(avail));  // open: gt, lt
  Comparator #(.width(16), .mode("unsigned")) comparator_5 (
    .a(addr), .b(16'h8004), .eq(read_en_keyboard));  // open: gt, lt
  Comparator #(.width(16), .mode("unsigned")) comparator_6 (
    .a(addr), .b(16'h8002), .eq(write_en_tty2));  // open: gt, lt
  Comparator #(.width(16), .mode("unsigned")) comparator_7 (
    .a(addr), .b(16'h8000), .eq(write_en_tty1));  // open: gt, lt
  // RAM ram_1: pin names not known; wires that end beside it: addr, word, dmplxr, clk, r_w_prime, data
  and and_3 (io_en, addr[15], mem);
  and and_4 (dmplxr, ~addr[15], mem);  // AND_Gate
  Random random_1 (.clk(clk), .next(random), .out(random_1_out));  // open: clr
  assign bit_extender_3_out = {{8{1'b0}}, random_1_out};  // Bit_Extender bit_extender_3
  and and_5 (and_5_out, io_en, r_w_prime, random);
  assign data = and_5_out ? bit_extender_3_out : 16'bz;  // Controlled_Buffer controlled_buffer_5
  TTY #(.rows(16)) tty_1 (.data(data[6:0]), .clk(clk), .we(and_6_out), .clr(and_7_out));
  and and_6 (and_6_out, write_en_tty1, ~r_w_prime, io_en);  // AND_Gate
  and and_7 (and_7_out, clr_tty1, r_w_prime, io_en);
  TTY #(.rows(16)) tty_2 (.data(data[6:0]), .clk(clk), .we(and_8_out), .clr(and_9_out));
  and and_8 (and_8_out, write_en_tty2, ~r_w_prime, io_en);  // AND_Gate
  and and_9 (and_9_out, clr_tty2, r_w_prime, io_en);

  // Other names for the same wires on the sheet: data0_6[6:0] = data[6:0]
endmodule
